// Logisim project SAP.circ as structural Verilog
module main (
);

  wire adder_1_cout, and_1_out, Ce, Ci, Cl, clock_1_out, Cm, Cn, controlled_buffer_2_out,
       controlled_buffer_6_out, Cy, Cz, De, demultiplexer_1_out0, demultiplexer_1_out1, demultiplexer_1_out2,
       demultiplexer_1_out3, demultiplexer_1_out4, demultiplexer_1_out5, demultiplexer_1_out6,
       demultiplexer_1_out7, demultiplexer_1_out8, demultiplexer_1_out9, demultiplexer_1_out10,
       demultiplexer_1_out11, demultiplexer_1_out12, demultiplexer_1_out13, demultiplexer_1_out14,
       demultiplexer_1_out15, demultiplexer_2_out0, demultiplexer_2_out1, demultiplexer_2_out2,
       demultiplexer_2_out3, demultiplexer_2_out4, demultiplexer_2_out5, demultiplexer_2_out6,
       demultiplexer_2_out7, demultiplexer_2_out8, demultiplexer_2_out9, demultiplexer_2_out10,
       demultiplexer_2_out11, demultiplexer_2_out12, demultiplexer_2_out13, demultiplexer_2_out14,
       demultiplexer_2_out15, Dl, Dw, Ea, Eb, Ec, Ee, Ef, Eu, HLT, La, Lb, Lc, Le, Lo, Lu, Ml, NOP_out,
       not_1_out, not_2_out, not_3_out, not_4_out, not_5_out, not_6_out, not_7_out, not_8_out, or_1_out,
       or_2_out, or_3_out, Pe, Pi, Pl, Ps, Ra, Re, Reset_out, Rl, shift_register_1_out, shift_register_1_q0,
       shift_register_1_q3, Su, subtractor_1_bout;
  wire [2:0] and_2_out;
  wire [3:0] SC_q;
  wire [7:0] ADR_q, controlled_buffer_21_out, F_q, IR_q;
  wire [14:0] controlled_buffer_8_out;
  wire [15:0] A_q, adder_1_out, B_q, C_q, controlled_buffer_1_out, controlled_buffer_9_out,
       controlled_buffer_15_out, controlled_buffer_16_out, controlled_buffer_18_out,
       controlled_buffer_19_out, D_q, E_q, MAR_q, O_q, PC_q, register_1_q, register_2_q, register_3_q,
       register_4_q, register_5_q, register_6_q, register_7_q, register_8_q, register_9_q, register_10_q,
       register_11_q, register_12_q, register_13_q, register_14_q, register_15_q, register_16_q,
       register_17_q, subtractor_1_out, U_q;

  assign controlled_buffer_1_out = Ra ? {and_2_out[1], controlled_buffer_8_out} : 16'bz;  // Controlled_Buffer controlled_buffer_1
  not not_1 (not_1_out, HLT);
  Shift_Register #(.length(7)) shift_register_1 (
    .shift(not_1_out), .in(shift_register_1_out), .clk(or_3_out), .out(shift_register_1_out),
    .load(or_1_out), .d0(1'b1), .q0(shift_register_1_q0), .d1(1'b0), .d2(1'b0), .d3(1'b0),
    .q3(shift_register_1_q3), .d4(1'b0), .d5(1'b0), .d6(1'b0));  // open: clr, q1, q2, q4, q5, q6
  Button Reset (.out(Reset_out));
  Register IR (.D(controlled_buffer_1_out[7:0]), .en(Ra), .Q(IR_q), .clk(or_3_out), .clr(Reset_out));
  Counter #(.trigger("falling")) ADR (
    .load(shift_register_1_q3), .D(IR_q), .count(not_1_out), .Q(ADR_q), .clk(or_3_out),
    .clr(shift_register_1_q0));  // open: carry, up
  RAM #(.addrWidth(16), .dataWidth(16), .databus("bidir"), .trigger("high")) Program_RAM (
    .addr(MAR_q), .we(Rl), .oe(Re), .clk(not_2_out));  // open: data
  Register #(.width(16)) MAR (
    .D({and_2_out[1], controlled_buffer_8_out}), .en(Ml), .Q(MAR_q), .clk(not_2_out), .clr(Reset_out));
  not not_2 (not_2_out, or_3_out);
  ROM #(.dataWidth(32)) Control_ROM (
    .addr(ADR_q),
    .data({Cn, Cy, Cm, Pi, Ps, Pe, Pl, HLT, Ec, Lc, Lu, Lo, Ee, Le, Ef, Cz, Dl, Dw, Ea, La, Eb, Lb, Su, Eu, Cl, Ci, Ce, Rl, Re, Ra, De, Ml}));
  or or_1 (or_1_out, NOP_out, Reset_out);
  assign controlled_buffer_2_out = Cy ? controlled_buffer_21_out[2] : 1'bz;  // Controlled_Buffer controlled_buffer_2
  assign controlled_buffer_2_out = Cn ? controlled_buffer_21_out[1] : 1'bz;  // Controlled_Buffer controlled_buffer_3
  assign controlled_buffer_2_out = Cm ? not_3_out : 1'bz;  // Controlled_Buffer controlled_buffer_4
  not not_3 (not_3_out, controlled_buffer_21_out[0]);
  assign controlled_buffer_2_out = Cz ? controlled_buffer_21_out[0] : 1'bz;  // Controlled_Buffer controlled_buffer_5
  or or_2 (or_2_out, Cy, Cn, Cm, Cz);
  assign controlled_buffer_6_out = or_2_out ? controlled_buffer_2_out : 1'bz;  // Controlled_Buffer controlled_buffer_6
  not not_4 (not_4_out, or_2_out);
  assign controlled_buffer_6_out = not_4_out ? Cl : 1'bz;  // Controlled_Buffer controlled_buffer_7
  PLA #(.in_width(32), .out_width(1), .\table ("00000000000000000000000000000000 1")) NOP (
    .in({Cn, Cy, Cm, Pi, Ps, Pe, Pl, HLT, Ec, Lc, Lu, Lo, Ee, Le, Ef, Cz, Dl, Dw, Ea, La, Eb, Lb, Su, Eu, Cl, Ci, Ce, Rl, Re, Ra, De, Ml}),
    .out(NOP_out));
  Counter #(.max('hffff), .width(16)) PC (
    .load(controlled_buffer_6_out), .D({and_2_out[1], controlled_buffer_8_out}), .count(Ci), .Q(PC_q),
    .clk(not_6_out), .clr(Reset_out));  // open: carry, up
  not not_5 (not_5_out, Dl);
  Clock clock_1 (.out(clock_1_out));
  or or_3 (or_3_out, clock_1_out, Reset_out);
  assign {and_2_out[1], controlled_buffer_8_out} = Ce ? register_1_q : 16'bz;  // Controlled_Buffer controlled_buffer_8
  Register #(.width(16)) register_1 (.D(PC_q), .Q(register_1_q), .clk(not_6_out), .clr(Reset_out));  // open: en
  not not_6 (not_6_out, or_3_out);
  assign controlled_buffer_9_out = and_1_out ? {and_2_out[1], controlled_buffer_8_out} : 16'bz;  // Controlled_Buffer controlled_buffer_9
  and and_1 (and_1_out, not_5_out, or_3_out);
  assign {and_2_out[1], controlled_buffer_8_out} = Dl ? D_q : 16'bz;  // Controlled_Buffer controlled_buffer_10
  Register #(.width(16)) D (.D(controlled_buffer_9_out), .en(De), .Q(D_q), .clk(or_3_out), .clr(Reset_out));
  assign {and_2_out[1], controlled_buffer_8_out} = Ea ? controlled_buffer_15_out : 16'bz;  // Controlled_Buffer controlled_buffer_11
  assign {and_2_out[1], controlled_buffer_8_out} = Eb ? controlled_buffer_16_out : 16'bz;  // Controlled_Buffer controlled_buffer_12
  assign {and_2_out[1], controlled_buffer_8_out} = Ec ? controlled_buffer_16_out : 16'bz;  // Controlled_Buffer controlled_buffer_13
  assign {and_2_out[1], controlled_buffer_8_out} = Ee ? controlled_buffer_18_out : 16'bz;  // Controlled_Buffer controlled_buffer_14
  assign controlled_buffer_15_out = Ea ? A_q : 16'bz;  // Controlled_Buffer controlled_buffer_15
  Register #(.width(16)) A (
    .D({and_2_out[1], controlled_buffer_8_out}), .en(La), .Q(A_q), .clk(or_3_out), .clr(Reset_out));
  assign controlled_buffer_16_out = Eb ? B_q : 16'bz;  // Controlled_Buffer controlled_buffer_16
  Register #(.width(16)) B (
    .D({and_2_out[1], controlled_buffer_8_out}), .en(Lb), .Q(B_q), .clk(or_3_out), .clr(Reset_out));
  assign controlled_buffer_16_out = Ec ? C_q : 16'bz;  // Controlled_Buffer controlled_buffer_17
  Register #(.width(16)) C (
    .D({and_2_out[1], controlled_buffer_8_out}), .en(Lc), .Q(C_q), .clk(or_3_out), .clr(Reset_out));
  Register #(.width(16)) O (
    .D({and_2_out[1], controlled_buffer_8_out}), .en(Lo), .Q(O_q), .clk(or_3_out), .clr(Reset_out));
  assign controlled_buffer_18_out = Ee ? E_q : 16'bz;  // Controlled_Buffer controlled_buffer_18
  Register #(.width(16)) E (
    .D({and_2_out[1], controlled_buffer_8_out}), .en(Le), .Q(E_q), .clk(or_3_out), .clr(Reset_out));
  Adder #(.width(16)) adder_1 (
    .a(controlled_buffer_15_out), .b(controlled_buffer_16_out), .out(adder_1_out), .cout(adder_1_cout));  // open: cin
  not not_7 (not_7_out, Su);
  Subtractor #(.width(16)) subtractor_1 (
    .a(controlled_buffer_15_out), .b(controlled_buffer_16_out), .out(subtractor_1_out),
    .bout(subtractor_1_bout));  // open: bin
  Hex_Digit_Display hex_digit_display_1 (.value(O_q[15:12]));  // open: dp
  assign controlled_buffer_19_out = not_7_out ? adder_1_out : 16'bz;  // Controlled_Buffer controlled_buffer_19
  Register #(.width(16)) U (.D(controlled_buffer_19_out), .en(Lu), .Q(U_q), .clk(or_3_out), .clr(Reset_out));
  assign controlled_buffer_19_out = Su ? subtractor_1_out : 16'bz;  // Controlled_Buffer controlled_buffer_20
  assign controlled_buffer_21_out = Ef ? F_q : 8'bz;  // Controlled_Buffer controlled_buffer_21
  Register F (.D({{5{1'b0}}, and_2_out}), .en(Eu), .Q(F_q), .clk(or_3_out), .clr(Reset_out));
  Hex_Digit_Display hex_digit_display_2 (.value(O_q[11:8]));  // open: dp
  Hex_Digit_Display hex_digit_display_3 (.value(O_q[7:4]));  // open: dp
  // Probe on O_q
  assign {and_2_out[1], controlled_buffer_8_out} = Eu ? U_q : 16'bz;  // Controlled_Buffer controlled_buffer_22
  assign and_2_out[2] = not_8_out ? adder_1_cout : 1'bz;  // Controlled_Buffer controlled_buffer_23
  assign and_2_out[2] = Su ? subtractor_1_bout : 1'bz;  // Controlled_Buffer controlled_buffer_24
  not not_8 (not_8_out, Su);
  Hex_Digit_Display hex_digit_display_4 (.value(O_q[3:0]));  // open: dp
  and and_2 (and_2_out[0], 1'b1, ~controlled_buffer_8_out[0], ~controlled_buffer_8_out[1], ~controlled_buffer_8_out[2], ~controlled_buffer_8_out[3], ~controlled_buffer_8_out[4], ~controlled_buffer_8_out[5], ~controlled_buffer_8_out[6], ~controlled_buffer_8_out[7], ~controlled_buffer_8_out[8], ~controlled_buffer_8_out[9], ~controlled_buffer_8_out[10], ~controlled_buffer_8_out[11], ~controlled_buffer_8_out[12], ~controlled_buffer_8_out[13], ~controlled_buffer_8_out[14], ~and_2_out[1]);  // AND_Gate
  Demultiplexer #(.enable("true"), .select(4)) demultiplexer_1 (
    .out0(demultiplexer_1_out0), .out1(demultiplexer_1_out1), .out2(demultiplexer_1_out2),
    .out3(demultiplexer_1_out3), .out4(demultiplexer_1_out4), .out5(demultiplexer_1_out5),
    .out6(demultiplexer_1_out6), .out7(demultiplexer_1_out7), .out8(demultiplexer_1_out8),
    .out9(demultiplexer_1_out9), .out10(demultiplexer_1_out10), .out11(demultiplexer_1_out11),
    .out12(demultiplexer_1_out12), .out13(demultiplexer_1_out13), .out14(demultiplexer_1_out14),
    .out15(demultiplexer_1_out15), .in(1'b1), .sel(SC_q), .en(Pe));
  assign {and_2_out[1], controlled_buffer_8_out} = demultiplexer_2_out0 ? register_2_q : 16'bz;  // Controlled_Buffer controlled_buffer_25
  Register #(.width(16)) register_2 (
    .D({and_2_out[1], controlled_buffer_8_out}), .en(demultiplexer_1_out0), .Q(register_2_q), .clk(or_3_out),
    .clr(Reset_out));
  assign {and_2_out[1], controlled_buffer_8_out} = demultiplexer_2_out1 ? register_3_q : 16'bz;  // Controlled_Buffer controlled_buffer_26
  Register #(.width(16)) register_3 (
    .D({and_2_out[1], controlled_buffer_8_out}), .en(demultiplexer_1_out1), .Q(register_3_q), .clk(or_3_out),
    .clr(Reset_out));
  assign {and_2_out[1], controlled_buffer_8_out} = demultiplexer_2_out2 ? register_4_q : 16'bz;  // Controlled_Buffer controlled_buffer_27
  Register #(.width(16)) register_4 (
    .D({and_2_out[1], controlled_buffer_8_out}), .en(demultiplexer_1_out2), .Q(register_4_q), .clk(or_3_out),
    .clr(Reset_out));
  assign {and_2_out[1], controlled_buffer_8_out} = demultiplexer_2_out3 ? register_5_q : 16'bz;  // Controlled_Buffer controlled_buffer_28
  Register #(.width(16)) register_5 (
    .D({and_2_out[1], controlled_buffer_8_out}), .en(demultiplexer_1_out3), .Q(register_5_q), .clk(or_3_out),
    .clr(Reset_out));
  assign {and_2_out[1], controlled_buffer_8_out} = demultiplexer_2_out4 ? register_6_q : 16'bz;  // Controlled_Buffer controlled_buffer_29
  Register #(.width(16)) register_6 (
    .D({and_2_out[1], controlled_buffer_8_out}), .en(demultiplexer_1_out4), .Q(register_6_q), .clk(or_3_out),
    .clr(Reset_out));
  assign {and_2_out[1], controlled_buffer_8_out} = demultiplexer_2_out5 ? register_7_q : 16'bz;  // Controlled_Buffer controlled_buffer_30
  Register #(.width(16)) register_7 (
    .D({and_2_out[1], controlled_buffer_8_out}), .en(demultiplexer_1_out5), .Q(register_7_q), .clk(or_3_out),
    .clr(Reset_out));
  assign {and_2_out[1], controlled_buffer_8_out} = demultiplexer_2_out6 ? register_8_q : 16'bz;  // Controlled_Buffer controlled_buffer_31
  Register #(.width(16)) register_8 (
    .D({and_2_out[1], controlled_buffer_8_out}), .en(demultiplexer_1_out6), .Q(register_8_q), .clk(or_3_out),
    .clr(Reset_out));
  assign {and_2_out[1], controlled_buffer_8_out} = demultiplexer_2_out7 ? register_9_q : 16'bz;  // Controlled_Buffer controlled_buffer_32
  Register #(.width(16)) register_9 (
    .D({and_2_out[1], controlled_buffer_8_out}), .en(demultiplexer_1_out7), .Q(register_9_q), .clk(or_3_out),
    .clr(Reset_out));
  assign {and_2_out[1], controlled_buffer_8_out} = demultiplexer_2_out8 ? register_10_q : 16'bz;  // Controlled_Buffer controlled_buffer_33
  Register #(.width(16)) register_10 (
    .D({and_2_out[1], controlled_buffer_8_out}), .en(demultiplexer_1_out8), .Q(register_10_q),
    .clk(or_3_out), .clr(Reset_out));
  assign {and_2_out[1], controlled_buffer_8_out} = demultiplexer_2_out9 ? register_11_q : 16'bz;  // Controlled_Buffer controlled_buffer_34
  Register #(.width(16)) register_11 (
    .D({and_2_out[1], controlled_buffer_8_out}), .en(demultiplexer_1_out9), .Q(register_11_q),
    .clk(or_3_out), .clr(Reset_out));
  assign {and_2_out[1], controlled_buffer_8_out} = demultiplexer_2_out10 ? register_12_q : 16'bz;  // Controlled_Buffer controlled_buffer_35
  Register #(.width(16)) register_12 (
    .D({and_2_out[1], controlled_buffer_8_out}), .en(demultiplexer_1_out10), .Q(register_12_q),
    .clk(or_3_out), .clr(Reset_out));
  assign {and_2_out[1], controlled_buffer_8_out} = demultiplexer_2_out11 ? register_13_q : 16'bz;  // Controlled_Buffer controlled_buffer_36
  Register #(.width(16)) register_13 (
    .D({and_2_out[1], controlled_buffer_8_out}), .en(demultiplexer_1_out11), .Q(register_13_q),
    .clk(or_3_out), .clr(Reset_out));
  assign {and_2_out[1], controlled_buffer_8_out} = demultiplexer_2_out12 ? register_14_q : 16'bz;  // Controlled_Buffer controlled_buffer_37
  Register #(.width(16)) register_14 (
    .D({and_2_out[1], controlled_buffer_8_out}), .en(demultiplexer_1_out12), .Q(register_14_q),
    .clk(or_3_out), .clr(Reset_out));
  assign {and_2_out[1], controlled_buffer_8_out} = demultiplexer_2_out13 ? register_15_q : 16'bz;  // Controlled_Buffer controlled_buffer_38
  Register #(.width(16)) register_15 (
    .D({and_2_out[1], controlled_buffer_8_out}), .en(demultiplexer_1_out13), .Q(register_15_q),
    .clk(or_3_out), .clr(Reset_out));
  assign {and_2_out[1], controlled_buffer_8_out} = demultiplexer_2_out14 ? register_16_q : 16'bz;  // Controlled_Buffer controlled_buffer_39
  Register #(.width(16)) register_16 (
    .D({and_2_out[1], controlled_buffer_8_out}), .en(demultiplexer_1_out14), .Q(register_16_q),
    .clk(or_3_out), .clr(Reset_out));
  assign {and_2_out[1], controlled_buffer_8_out} = demultiplexer_2_out15 ? register_17_q : 16'bz;  // Controlled_Buffer controlled_buffer_40
  Register #(.width(16)) register_17 (
    .D({and_2_out[1], controlled_buffer_8_out}), .en(demultiplexer_1_out15), .Q(register_17_q),
    .clk(or_3_out), .clr(Reset_out));
  Demultiplexer #(.enable("true"), .select(4)) demultiplexer_2 (
    .out0(demultiplexer_2_out0), .out1(demultiplexer_2_out1), .out2(demultiplexer_2_out2),
    .out3(demultiplexer_2_out3), .out4(demultiplexer_2_out4), .out5(demultiplexer_2_out5),
    .out6(demultiplexer_2_out6), .out7(demultiplexer_2_out7), .out8(demultiplexer_2_out8),
    .out9(demultiplexer_2_out9), .out10(demultiplexer_2_out10), .out11(demultiplexer_2_out11),
    .out12(demultiplexer_2_out12), .out13(demultiplexer_2_out13), .out14(demultiplexer_2_out14),
    .out15(demultiplexer_2_out15), .in(1'b1), .sel(SC_q), .en(Pl));
  Counter #(.max('hf), .ongoal("stay"), .width(4)) SC (
    .count(Ps), .Q(SC_q), .up(Pi), .clk(or_3_out), .clr(Reset_out));  // open: load, D, carry

  // Notes on the sheet:
  //   contents of Control_ROM (hex, n*v repeats v):
  //   84 52 120 80000000 84 52 900 0 84 52 2100 0 84 52 20100 0 84 41400 8800 0 84 50400 8800 0 84 45400
  //   8800 0 84 54400 8800 0 84 52 180 408 84 52 180 1008 84 52 180 10008 84 80400 0 0 84 52 101 0 86
  //   200054 101 0 100001 0 0 0 84 52 c00100 0 84 52 1400100 0 c6 1d0 50 900 c6 1d0 50 2100 c6 1d0 50
  //   20100 84 52 2400100 0 84 52 4400100 0 2400 0 20400 0 1800 0 21000 0 10800 0 12000 0 18000000 0
  //   10000000 0 20000400 0 40000800 0 20001000 0 40002000 0 20010000 0 40020000
endmodule

module Adder1bit (
  input  A,
  input  B,
  input  CI,
  input  SUB,
  output S,
  output CO
);

  wire Q1_out, Q2_out, Q4_out, xor_1_out;

  xor xor_1 (xor_1_out, B, SUB);
  xor Q1 (Q1_out, A, xor_1_out);
  and Q2 (Q2_out, A, xor_1_out);
  xor Q3 (S, CI, Q1_out);
  and Q4 (Q4_out, Q1_out, CI);
  or Q5 (CO, Q4_out, Q2_out);
endmodule

// VHDL entity ALU, as the project stores it:
--------------------------------------------------------------------------------
-- Project :
-- File    :
-- Autor   :
-- Date    :
--
--------------------------------------------------------------------------------
-- Description :
--
--------------------------------------------------------------------------------

LIBRARY ieee;
USE ieee.std_logic_1164.all;

ENTITY ALU IS
  PORT (
  ------------------------------------------------------------------------------
  --Insert input ports below
    clock      : IN  std_logic;                    -- input bit example
    val        : IN  std_logic_vector(3 DOWNTO 0); -- input vector example
  ------------------------------------------------------------------------------
  --Insert output ports below
    max        : OUT std_logic;                    -- output bit example
    cpt        : OUT std_logic_vector(3 DOWNTO 0)  -- output vector example
    );
END ALU;

--------------------------------------------------------------------------------
--Complete your VHDL description below
--------------------------------------------------------------------------------

ARCHITECTURE TypeArchitecture OF ALU IS

BEGIN


END TypeArchitecture;
